// Logisim project CS1409_U201414810_杨卿_alu.circ as structural Verilog: 8 circuits, main circuit ALU
module ALU (
  input  [31:0] X,
  input  [31:0] Y,
  input  [3:0] AluOP,
  output Signed_Overflow,
  output UnSigned_Overflow,
  output Equal,
  output [31:0] Result,
  output [31:0] Result_2
);

  wire comparator_1_lt, comparator_2_lt, n32bits_1_c32, n32bits_1_of, n32bits_2_of;
  wire [4:0] bit_extender_1_out;
  wire [31:0] and_1_out, bit_extender_2_out, bit_extender_3_out, divider_1_out, divider_1_rem,
       multiplier_1_cout, multiplier_1_out, n32bits_1_s, n32bits_2_s, negator_1_out, nor_1_out, or_1_out,
       shifter_1_out, shifter_2_out, shifter_3_out, xor_1_out;

  // Probe on X
  // Probe on X
  // Probe on Y
  // Probe on Y
  // Probe on AluOP
  Bit_Extender #(.in_width(32), .out_width(5)) bit_extender_1 (.in(Y), .out(bit_extender_1_out));
  Negator #(.width(32)) negator_1 (.in(Y), .out(negator_1_out));
  // Probe on Result
  // Probe on Result
  Shifter #(.width(32)) shifter_1 (.in(X), .\dist (bit_extender_1_out), .out(shifter_1_out));
  Shifter #(.width(32), .shift("ar")) shifter_2 (.in(X), .\dist (bit_extender_1_out), .out(shifter_2_out));
  Shifter #(.width(32), .shift("lr")) shifter_3 (.in(X), .\dist (bit_extender_1_out), .out(shifter_3_out));
  Multiplier #(.width(32)) multiplier_1 (
    .a(X), .b(Y), .out(multiplier_1_out), .cin({32{1'b0}}), .cout(multiplier_1_cout));
  Divider #(.width(32)) divider_1 (.a(X), .b(Y), .out(divider_1_out), .upper({32{1'b0}}), .rem(divider_1_rem));
  _32bits u_32bits_1 (.OF(n32bits_1_of), .C0(1'b0), .C32(n32bits_1_c32), .S(n32bits_1_s), .in_2(X), .in_3(Y));
  _32bits u_32bits_2 (.OF(n32bits_2_of), .C0(1'b0), .S(n32bits_2_s), .in_2(X), .in_3(negator_1_out));  // open: C32
  assign and_1_out = X & Y;  // AND_Gate and_1, 32 bits wide
  assign or_1_out = X | Y;  // OR_Gate or_1, 32 bits wide
  assign xor_1_out = X ^ Y;  // XOR_Gate xor_1, 32 bits wide
  assign nor_1_out = ~(X | Y);  // NOR_Gate nor_1, 32 bits wide
  Comparator #(.width(32)) comparator_1 (.a(X), .b(Y), .lt(comparator_1_lt));  // open: gt, eq
  Comparator #(.width(32), .mode("unsigned")) comparator_2 (.a(X), .b(Y), .lt(comparator_2_lt));  // open: gt, eq
  Comparator #(.width(32)) comparator_3 (.a(X), .b(Y), .eq(Equal));  // open: gt, lt
  assign bit_extender_2_out = {{31{1'b0}}, comparator_1_lt};  // Bit_Extender bit_extender_2
  assign bit_extender_3_out = {{31{1'b0}}, comparator_2_lt};  // Bit_Extender bit_extender_3
  // Probe on Result_2
  Multiplexer #(.select(4), .width(32), .enable("false")) multiplexer_1 (
    .in0(shifter_1_out), .in1(shifter_2_out), .in2(shifter_3_out), .in3(multiplier_1_out),
    .in4(divider_1_out), .in5(n32bits_1_s), .in6(n32bits_2_s), .in7(and_1_out), .in8(or_1_out),
    .in9(xor_1_out), .in10(nor_1_out), .in11(bit_extender_2_out), .in12(bit_extender_3_out),
    .in13({32{1'b0}}), .in14({32{1'b0}}), .in15({32{1'b0}}), .out(Result), .sel(AluOP));
  Multiplexer #(.select(4), .width(32), .enable("false")) multiplexer_2 (
    .in0({32{1'b0}}), .in1({32{1'b0}}), .in2({32{1'b0}}), .in3(multiplier_1_cout), .in4(divider_1_rem),
    .in5({32{1'b0}}), .in6({32{1'b0}}), .in7({32{1'b0}}), .in8({32{1'b0}}), .in9({32{1'b0}}),
    .in10({32{1'b0}}), .in11({32{1'b0}}), .in12({32{1'b0}}), .in13({32{1'b0}}), .in14({32{1'b0}}),
    .in15({32{1'b0}}), .out(Result_2), .sel(AluOP));
  Multiplexer #(.select(4), .enable("false")) multiplexer_3 (
    .in0(1'b0), .in1(1'b0), .in2(1'b0), .in3(1'b0), .in4(1'b0), .in5(n32bits_1_of), .in6(n32bits_2_of),
    .in7(1'b0), .in8(1'b0), .in9(1'b0), .in10(1'b0), .in11(1'b0), .in12(1'b0), .in13(1'b0), .in14(1'b0),
    .in15(1'b0), .out(Signed_Overflow), .sel(AluOP));
  Multiplexer #(.select(4), .enable("false")) multiplexer_4 (
    .in0(1'b0), .in1(1'b0), .in2(1'b0), .in3(1'b0), .in4(1'b0), .in5(n32bits_1_c32), .in6(comparator_2_lt),
    .in7(1'b0), .in8(1'b0), .in9(1'b0), .in10(1'b0), .in11(1'b0), .in12(1'b0), .in13(1'b0), .in14(1'b0),
    .in15(1'b0), .out(UnSigned_Overflow), .sel(AluOP));

  // Other names for the same wires on the sheet: OF = Signed_Overflow; Result2[31:0] = Result_2; S[3:0] = AluOP;
  //   UOF = UnSigned_Overflow

  // Notes on the sheet:
  //   不要改变此引脚区域内容，也不要改变ALU封装形式
  //   输入引脚
  //   请在下方利用上方输入输出引脚的隧道信号构建ALU电路，ctrl+d复制选择部件
  //   华中科技大学计算机学院 计算机组成原理，鸣谢加州大学伯克利CS61C课程
  //   输出引脚
  //   探测区域
endmodule

module \演示电路  (
  input  [31:0] X,
  input  [31:0] Y,
  input  [3:0] ALUOP,
  output Signed_Overflow,
  output Unsigned_overflow,
  output [31:0] Result,
  output [31:0] Result_2,
  output Equal
);

  // Probe on X
  // Probe on X
  ALU alu_1 (
    .AluOP(ALUOP), .X(X), .Equal(Equal), .Result(Result), .Signed_Overflow(Signed_Overflow), .Y(Y),
    .Result_2(Result_2), .UnSigned_Overflow(Unsigned_overflow));
  // Probe on ALUOP
  // Probe on Y
  // Probe on Y
  // Probe on Result
  // Probe on Result
  // Probe on Result_2

  // Notes on the sheet:
  //   ALu电路无需调整位置即可连接在该电路中，并且不能出现蓝色线缆和三态输出
endmodule

module \等差数列  (
  input  [31:0] \数列初始值 ,
  input  [31:0] \等差值 ,
  input  \时钟 ,
  output [31:0] Result
);

  // Probe on \数列初始值 
  // Probe on \数列初始值 
  // Probe on \等差值 
  // Probe on \等差值 
  // Probe on Result
  // Probe on Result

  // Other names for the same wires on the sheet: 数列初值[31:0] = \数列初始值 ; 累加和[31:0] = Result

  // Notes on the sheet:
  //   不要改变此引脚区域内容，也不要改变ALU封装形式
  //   请在下方利用上方输入输出引脚的隧道信号构建等差数列求和电路，ctrl+d复制选择部件
  //   华中科技大学计算机学院 计算机组成原理，鸣谢加州大学伯克利CS61C课程
  //   输出引脚
  //   探测区域
endmodule

module _16bits (
  input  C0,
  input  [15:0] in_2,
  input  [15:0] in_3,
  output [15:0] S,
  output P_star,
  output G_star,
  output C15
);

  wire n74181_1_g_star, n74181_1_p_star, n74181_2_g_star, n74181_2_p_star, n74181_3_g_star, n74181_3_p_star,
       n74181_4_g_star, n74181_4_p_star, n74182_1_c1, n74182_1_c2, n74182_1_c3;

  _74181 u_74181_1 (
    .C3(C15), .P_star(n74181_1_p_star), .G_star(n74181_1_g_star), .S4(S[15]), .S3(S[14]), .S2(S[13]),
    .S1(S[12]), .X(in_2[15:12]), .Y(in_3[15:12]), .C0(n74182_1_c3));
  _74181 u_74181_2 (
    .P_star(n74181_2_p_star), .G_star(n74181_2_g_star), .S4(S[11]), .S3(S[10]), .S2(S[9]), .S1(S[8]),
    .X(in_2[11:8]), .Y(in_3[11:8]), .C0(n74182_1_c2));  // open: C3
  _74182 u_74182_1 (
    .P_star(P_star), .G_star(G_star), .C3(n74182_1_c3), .C2(n74182_1_c2), .C1(n74182_1_c1),
    .G4(n74181_1_g_star), .P4(n74181_1_p_star), .G3(n74181_2_g_star), .P3(n74181_2_p_star),
    .G2(n74181_3_g_star), .P2(n74181_3_p_star), .G1(n74181_4_g_star), .P1(n74181_4_p_star), .C0(C0));  // open: C4
  _74181 u_74181_3 (
    .P_star(n74181_3_p_star), .G_star(n74181_3_g_star), .S4(S[7]), .S3(S[6]), .S2(S[5]), .S1(S[4]),
    .X(in_2[7:4]), .Y(in_3[7:4]), .C0(n74182_1_c1));  // open: C3
  _74181 u_74181_4 (
    .P_star(n74181_4_p_star), .G_star(n74181_4_g_star), .S4(S[3]), .S3(S[2]), .S2(S[1]), .S1(S[0]),
    .X(in_2[3:0]), .Y(in_3[3:0]), .C0(C0));  // open: C3
endmodule

module _74181 (
  input  C0,
  input  [3:0] X,
  input  [3:0] Y,
  output S4,
  output S3,
  output S2,
  output S1,
  output C3,
  output P_star,
  output G_star
);

  wire generatepgsignal_1_g1, generatepgsignal_1_g2, generatepgsignal_1_g3, generatepgsignal_1_g4,
       generatepgsignal_1_p1, generatepgsignal_1_p2, generatepgsignal_1_p3, generatepgsignal_1_p4,
       n74182_1_c1, n74182_1_c2;

  xor xor_1 (S4, generatepgsignal_1_p4, C3);
  generatePGsignal generatepgsignal_1 (
    .G4(generatepgsignal_1_g4), .P4(generatepgsignal_1_p4), .G3(generatepgsignal_1_g3),
    .P3(generatepgsignal_1_p3), .G2(generatepgsignal_1_g2), .P2(generatepgsignal_1_p2),
    .G1(generatepgsignal_1_g1), .P1(generatepgsignal_1_p1), .in_1(X), .in_2(Y));
  xor xor_2 (S2, n74182_1_c1, generatepgsignal_1_p2);
  xor xor_3 (S3, n74182_1_c2, generatepgsignal_1_p3);
  _74182 u_74182_1 (
    .P_star(P_star), .G_star(G_star), .C3(C3), .C2(n74182_1_c2), .C1(n74182_1_c1),
    .G4(generatepgsignal_1_g4), .P4(generatepgsignal_1_p4), .G3(generatepgsignal_1_g3),
    .P3(generatepgsignal_1_p3), .G2(generatepgsignal_1_g2), .P2(generatepgsignal_1_p2),
    .G1(generatepgsignal_1_g1), .P1(generatepgsignal_1_p1), .C0(C0));  // open: C4
  xor xor_4 (S1, generatepgsignal_1_p1, C0);
endmodule

module _74182 (
  input  C0,
  input  G4,
  input  P4,
  input  G3,
  input  P3,
  input  G2,
  input  P2,
  input  G1,
  input  P1,
  output C4,
  output P_star,
  output G_star,
  output C3,
  output C2,
  output C1
);

  wire and_1_out, and_2_out, and_3_out, and_4_out, and_5_out, and_7_out, and_8_out, and_9_out, and_10_out,
       and_11_out;

  and and_1 (and_1_out, P4, G3);
  and and_2 (and_2_out, P4, P3, G2);
  or or_1 (G_star, G4, and_1_out, and_2_out, and_3_out);
  and and_3 (and_3_out, P4, P3, P2, G1);
  or or_2 (C4, G_star, and_4_out);
  and and_4 (and_4_out, P_star, C0);
  and and_5 (and_5_out, P3, G2);
  and and_6 (P_star, P4, P3, P2, P1);
  or or_3 (C3, G3, and_5_out, and_7_out, and_8_out);
  and and_7 (and_7_out, P3, P2, G1);
  and and_8 (and_8_out, P3, P2, P1, C0);
  or or_4 (C2, G2, and_9_out, and_10_out);
  and and_9 (and_9_out, P2, G1);
  and and_10 (and_10_out, P2, P1, C0);
  or or_5 (C1, G1, and_11_out);
  and and_11 (and_11_out, P1, C0);
endmodule

module generatePGsignal (
  input  [3:0] in_1,
  input  [3:0] in_2,
  output G4,
  output P4,
  output G3,
  output P3,
  output G2,
  output P2,
  output G1,
  output P1
);

  xor xor_1 (P4, in_1[3], in_2[3]);
  and and_1 (G4, in_1[3], in_2[3]);
  xor xor_2 (P3, in_1[2], in_2[2]);
  and and_2 (G3, in_1[2], in_2[2]);
  and and_3 (G2, in_1[1], in_2[1]);
  xor xor_3 (P2, in_1[1], in_2[1]);
  and and_4 (G1, in_1[0], in_2[0]);
  xor xor_4 (P1, in_1[0], in_2[0]);
endmodule

module _32bits (
  input  C0,
  input  [31:0] in_2,
  input  [31:0] in_3,
  output C32,
  output OF,
  output [31:0] S
);

  wire n16bits_1_c15, n16bits_1_g_star, n16bits_1_p_star, n16bits_2_g_star, n16bits_2_p_star, n74182_1_c1;

  xor xor_1 (OF, C32, n16bits_1_c15);
  _16bits u_16bits_1 (
    .P_star(n16bits_1_p_star), .G_star(n16bits_1_g_star), .C15(n16bits_1_c15), .S(S[31:16]),
    .in_2(in_2[31:16]), .in_3(in_3[31:16]), .C0(n74182_1_c1));
  _74182 u_74182_1 (
    .C2(C32), .C1(n74182_1_c1), .G4(1'b0), .P4(1'b0), .G3(1'b0), .P3(1'b0), .G2(n16bits_1_g_star),
    .P2(n16bits_1_p_star), .G1(n16bits_2_g_star), .P1(n16bits_2_p_star), .C0(C0));  // open: P_star, G_star, C4, C3
  _16bits u_16bits_2 (
    .P_star(n16bits_2_p_star), .G_star(n16bits_2_g_star), .S(S[15:0]), .in_2(in_2[15:0]), .in_3(in_3[15:0]),
    .C0(C0));  // open: C15
endmodule
