// Logisim project CS1409_U201414810_杨卿_regfile-1.circ as structural Verilog: 3 circuits, main circuit main
module main (
  input  [4:0] Reg1_num,
  input  [4:0] Reg2,
  input  [4:0] Write_Reg_num,
  input  [31:0] Din,
  input  Write_Enable,
  input  Clock,
  output [31:0] Reg1,
  output [31:0] a0_Value,
  output [31:0] v0_Value,
  output [31:0] s2_Value,
  output [31:0] ra_Value,
  output [31:0] Reg2_2
);

  wire [7:0] decoder_1_out0, decoder_1_out8, decoder_1_out16, decoder_1_out24;
  wire [31:0] _1, _3, _5, _6, _7, _8, _9, _10, _11, _12, _13, _14, _15, _16, _17, _19, _20, _21, _22, _23,
       _24, _25, _26, _27, _28, _29, _30;

  Decoder #(.select(5), .disabled(0)) decoder_1 (
    .out0(decoder_1_out0[0]), .out1(decoder_1_out0[1]), .out2(decoder_1_out0[2]), .out3(decoder_1_out0[3]),
    .out4(decoder_1_out0[4]), .out5(decoder_1_out0[5]), .out6(decoder_1_out0[6]), .out7(decoder_1_out0[7]),
    .out8(decoder_1_out8[0]), .out9(decoder_1_out8[1]), .out10(decoder_1_out8[2]), .out11(decoder_1_out8[3]),
    .out12(decoder_1_out8[4]), .out13(decoder_1_out8[5]), .out14(decoder_1_out8[6]),
    .out15(decoder_1_out8[7]), .out16(decoder_1_out16[0]), .out17(decoder_1_out16[1]),
    .out18(decoder_1_out16[2]), .out19(decoder_1_out16[3]), .out20(decoder_1_out16[4]),
    .out21(decoder_1_out16[5]), .out22(decoder_1_out16[6]), .out23(decoder_1_out16[7]),
    .out24(decoder_1_out24[0]), .out25(decoder_1_out24[1]), .out26(decoder_1_out24[2]),
    .out27(decoder_1_out24[3]), .out28(decoder_1_out24[4]), .out29(decoder_1_out24[5]),
    .out30(decoder_1_out24[6]), .out31(decoder_1_out24[7]), .sel(Write_Reg_num), .en(Write_Enable));
  Register #(.width(32), .trigger("falling")) u__8 (.D(Din), .en(decoder_1_out8[0]), .Q(_8), .clk(Clock));  // open: clr
  Register #(.width(32), .trigger("falling")) u__16 (
    .D(Din), .en(decoder_1_out16[0]), .Q(_16), .clk(Clock));  // open: clr
  Register #(.width(32), .trigger("falling")) u__24 (
    .D(Din), .en(decoder_1_out24[0]), .Q(_24), .clk(Clock));  // open: clr
  Register #(.width(32), .trigger("falling")) u__1 (.D(Din), .en(decoder_1_out0[1]), .Q(_1), .clk(Clock));  // open: clr
  Register #(.width(32), .trigger("falling")) u__9 (.D(Din), .en(decoder_1_out8[1]), .Q(_9), .clk(Clock));  // open: clr
  Register #(.width(32), .trigger("falling")) u__17 (
    .D(Din), .en(decoder_1_out16[1]), .Q(_17), .clk(Clock));  // open: clr
  Register #(.width(32), .trigger("falling")) u__25 (
    .D(Din), .en(decoder_1_out24[1]), .Q(_25), .clk(Clock));  // open: clr
  Register #(.width(32), .trigger("falling")) _2 (
    .D(Din), .en(decoder_1_out0[2]), .Q(v0_Value), .clk(Clock));  // open: clr
  Register #(.width(32), .trigger("falling")) u__10 (
    .D(Din), .en(decoder_1_out8[2]), .Q(_10), .clk(Clock));  // open: clr
  Register #(.width(32), .trigger("falling")) _18 (
    .D(Din), .en(decoder_1_out16[2]), .Q(s2_Value), .clk(Clock));  // open: clr
  Register #(.width(32), .trigger("falling")) u__26 (
    .D(Din), .en(decoder_1_out24[2]), .Q(_26), .clk(Clock));  // open: clr
  Register #(.width(32), .trigger("falling")) u__3 (.D(Din), .en(decoder_1_out0[3]), .Q(_3), .clk(Clock));  // open: clr
  Register #(.width(32), .trigger("falling")) u__11 (
    .D(Din), .en(decoder_1_out8[3]), .Q(_11), .clk(Clock));  // open: clr
  Register #(.width(32), .trigger("falling")) u__19 (
    .D(Din), .en(decoder_1_out16[3]), .Q(_19), .clk(Clock));  // open: clr
  Register #(.width(32), .trigger("high")) u__27 (.D(Din), .en(decoder_1_out24[3]), .Q(_27), .clk(Clock));  // open: clr
  Register #(.width(32), .trigger("falling")) _4 (
    .D(Din), .en(decoder_1_out0[4]), .Q(a0_Value), .clk(Clock));  // open: clr
  Register #(.width(32), .trigger("falling")) u__12 (
    .D(Din), .en(decoder_1_out8[4]), .Q(_12), .clk(Clock));  // open: clr
  Register #(.width(32), .trigger("falling")) u__20 (
    .D(Din), .en(decoder_1_out16[4]), .Q(_20), .clk(Clock));  // open: clr
  Register #(.width(32), .trigger("falling")) u__28 (
    .D(Din), .en(decoder_1_out24[4]), .Q(_28), .clk(Clock));  // open: clr
  Register #(.width(32), .trigger("falling")) u__5 (.D(Din), .en(decoder_1_out0[5]), .Q(_5), .clk(Clock));  // open: clr
  Register #(.width(32), .trigger("falling")) u__13 (
    .D(Din), .en(decoder_1_out8[5]), .Q(_13), .clk(Clock));  // open: clr
  Register #(.width(32), .trigger("falling")) u__21 (
    .D(Din), .en(decoder_1_out16[5]), .Q(_21), .clk(Clock));  // open: clr
  Register #(.width(32), .trigger("falling")) u__29 (
    .D(Din), .en(decoder_1_out24[5]), .Q(_29), .clk(Clock));  // open: clr
  Register #(.width(32), .trigger("falling")) u__6 (.D(Din), .en(decoder_1_out0[6]), .Q(_6), .clk(Clock));  // open: clr
  Register #(.width(32), .trigger("falling")) u__14 (
    .D(Din), .en(decoder_1_out8[6]), .Q(_14), .clk(Clock));  // open: clr
  Register #(.width(32), .trigger("falling")) u__22 (
    .D(Din), .en(decoder_1_out16[6]), .Q(_22), .clk(Clock));  // open: clr
  Register #(.width(32), .trigger("falling")) u__30 (
    .D(Din), .en(decoder_1_out24[6]), .Q(_30), .clk(Clock));  // open: clr
  Register #(.width(32), .trigger("falling")) u__7 (.D(Din), .en(decoder_1_out0[7]), .Q(_7), .clk(Clock));  // open: clr
  Register #(.width(32), .trigger("falling")) u__15 (
    .D(Din), .en(decoder_1_out8[7]), .Q(_15), .clk(Clock));  // open: clr
  Register #(.width(32), .trigger("falling")) u__23 (
    .D(Din), .en(decoder_1_out16[7]), .Q(_23), .clk(Clock));  // open: clr
  Register #(.width(32), .trigger("falling")) _31 (
    .D(Din), .en(decoder_1_out24[7]), .Q(ra_Value), .clk(Clock));  // open: clr
  Multiplexer #(.select(5), .width(32), .enable("false")) multiplexer_1 (
    .in0({32{1'b0}}), .in1(_1), .in2(v0_Value), .in3(_3), .in4(a0_Value), .in5(_5), .in6(_6), .in7(_7),
    .in8(_8), .in9(_9), .in10(_10), .in11(_11), .in12(_12), .in13(_13), .in14(_14), .in15(_15), .in16(_16),
    .in17(_17), .in18(s2_Value), .in19(_19), .in20(_20), .in21(_21), .in22(_22), .in23(_23), .in24(_24),
    .in25(_25), .in26(_26), .in27(_27), .in28(_28), .in29(_29), .in30(_30), .in31(ra_Value), .out(Reg1),
    .sel(Reg1_num));
  Multiplexer #(.select(5), .width(32), .enable("false")) multiplexer_2 (
    .in0({32{1'b0}}), .in1(_1), .in2(v0_Value), .in3(_3), .in4(a0_Value), .in5(_5), .in6(_6), .in7(_7),
    .in8(_8), .in9(_9), .in10(_10), .in11(_11), .in12(_12), .in13(_13), .in14(_14), .in15(_15), .in16(_16),
    .in17(_17), .in18(s2_Value), .in19(_19), .in20(_20), .in21(_21), .in22(_22), .in23(_23), .in24(_24),
    .in25(_25), .in26(_26), .in27(_27), .in28(_28), .in29(_29), .in30(_30), .in31(ra_Value), .out(Reg2_2),
    .sel(Reg2));

  // Other names for the same wires on the sheet: _2[31:0] = v0_Value; v0[31:0] = v0_Value; _4[31:0] = a0_Value;
  //   a0[31:0] = a0_Value; _18[31:0] = s2_Value; s2[31:0] = s2_Value; _31[31:0] = ra_Value; ra[31:0] = ra_Value;
  //   clk = Clock; reg2_num[4:0] = Reg2; reg2_t[31:0] = Reg2_2; WE = Write_Enable; write_data[31:0] = Din

  // Notes on the sheet:
  //   输入引脚
  //   输出引脚
  //   0
  //   Debug引脚，便于观测寄存器值
  //   请勿修改引脚以及封装，直接使用隧道连接电路
endmodule

module test (
);

  wire undriven;

  main main_1 (.Clock(undriven));  // open: Reg1_num, Reg2, Write_Reg_num, Din, Write_Enable, Reg1, Reg2_2, a0_Value, v0_Value, s2_Value, ra_Value
endmodule

module \自动运算电路  (
);

  wire clock_1_out, counter_2_q, counter_3_carry, counter_4_q, counter_5_q, multiplexer_1_out;
  wire [3:0] alu_1_result;
  wire [4:0] counter_3_q;
  wire [5:5] counter_1_q;
  wire [31:0] main_1_ra_value, ram_1_data;
  wire [31:4] alu_1_result_2;

  Clock clock_1 (.out(clock_1_out));
  Multiplexer #(.disabled(0), .enable("false")) multiplexer_1 (
    .in0(clock_1_out), .in1(1'b0), .out(multiplexer_1_out), .sel(counter_3_carry));
  Counter #(.width(1), .max('h1)) counter_1 (
    .D(1'b0), .Q(counter_1_q[5]), .clk(multiplexer_1_out), .clr(1'b0));  // open: load, count, carry
  Counter #(.width(1), .max('h1)) counter_2 (
    .D(1'b0), .Q(counter_2_q), .clk(multiplexer_1_out), .clr(1'b0));  // open: load, count, carry
  Counter #(.width(5), .max('h1f), .trigger("falling")) counter_3 (
    .D({5{1'b0}}), .Q(counter_3_q), .carry(counter_3_carry), .clk(counter_2_q), .clr(1'b0));  // open: load, count
  Counter #(.width(1), .max('h1)) counter_4 (
    .D(1'b0), .Q(counter_4_q), .clk(multiplexer_1_out));  // open: load, count, carry, clr
  Counter #(.width(1), .max('h1)) counter_5 (
    .D(1'b0), .Q(counter_5_q), .clk(multiplexer_1_out));  // open: load, count, carry, clr
  RAM #(.addrWidth(6), .dataWidth(32), .bus("separate")) ram_1 (
    .addr({counter_1_q[5], counter_3_q}), .din({alu_1_result_2, alu_1_result}), .data(ram_1_data),
    .str(1'b1), .sel(1'b1), .clk(counter_4_q), .ld(1'b1), .clr(1'b0));
  // Probe on ram_1_data
  main main_1 (
    .Write_Reg_num({5{1'b1}}), .Din({alu_1_result_2, alu_1_result}), .Write_Enable(1'b1),
    .Clock(counter_5_q), .ra_Value(main_1_ra_value));  // open: Reg1_num, Reg2, Reg1, Reg2_2, a0_Value, v0_Value, s2_Value
  ALU alu_1 (
    .AluOP(4'b0101), .X(ram_1_data), .Result({alu_1_result_2, alu_1_result}), .Y(main_1_ra_value));  // open: Equal, Signed_Overflow, Result_2, UnSigned_Overflow
  // Probe on main_1_ra_value
  Hex_Digit_Display hex_digit_display_1 (.value(alu_1_result_2[31:28]));  // open: dp
  Hex_Digit_Display hex_digit_display_2 (.value(alu_1_result_2[27:24]));  // open: dp
  Hex_Digit_Display hex_digit_display_3 (.value(alu_1_result_2[19:16]));  // open: dp
  Hex_Digit_Display hex_digit_display_4 (.value(alu_1_result_2[23:20]));  // open: dp
  Hex_Digit_Display hex_digit_display_5 (.value(alu_1_result_2[15:12]));  // open: dp
  Hex_Digit_Display hex_digit_display_6 (.value(alu_1_result_2[11:8]));  // open: dp
  Hex_Digit_Display hex_digit_display_7 (.value(alu_1_result_2[7:4]));  // open: dp
  Hex_Digit_Display hex_digit_display_8 (.value(alu_1_result));  // open: dp
endmodule
