// Logisim project 流水中断_MIPS_CPU .circ as structural Verilog: 11 circuits, main circuit Control Unit
// loaduse
module main (
);

  wire and_1_out, and_2_out, and_3_out, BeqEX, BeqID, BgezEX, BgezID, BJEEX, BneEX, BneID, BranchorJump,
       BranchSuccessEX, clk, clk1, clock_1_out, clr1, clr2, comparator_1_eq, enable3, EretEX, EretID,
       ex_mem_1_jalmem, ex_mem_1_syscallmem, ex_mem_1_weex_2, ExpSrc1, ExpSrc2, ExpSrc3, geEX, HaltWB,
       HasExp, HighMEM, id_ex_1_jalex, id_ex_1_shex, id_ex_1_swex, id_ex_1_syscallex, id_ex_1_weex, \I型ID ,
       J_jalEX, J_jalID, JalID, JalWB, JrEX, JrID, loaduse, LwEX, LwID, LwMEM, LwWB, Mfc0EX, Mfc0ID, Mfc0MEM,
       Mfc0WB, Mtc0EX, Mtc0ID, multiplexer_4_out, not_1_out, or_1_out, or_2_out, RedrectR1MEM,
       RedrectR1MEM_num, RedrectR1WB, RedrectR1WB_num, RedrectR2MEM, RedrectR2MEM_num, RedrectR2WB,
       RedrectR2WB_num, \R型ID , select1ID, select2EX, select2ID, select3ID, ShID, ShiftEX, ShiftID, ShMEM,
       SwID, SwMEM, SyscaID, SyscallWB, WeID, WeWB, ZeroEX, \跳转型ID ;
  wire [1:0] cp0regID_num, cp0regwriteEX;
  wire [3:0] AluopEX, AluopID;
  wire [4:0] multiplexer_8_out, R1, R1ID_num, R2ID_num, RW_num, WriteRegEX, WriteRegID, WriteRegMEM,
       WriteRegWB;
  wire [8:0] demultiplexer_1_out0, demultiplexer_1_out1;
  wire [15:0] counter_1_q, counter_2_q, counter_3_q, counter_4_q, counter_5_q, counter_6_q, ram_1_data,
       ram_1_data_2;
  wire [27:0] shifter_1_out;
  wire [31:0] a0, adder_1_out, adder_2_out, ALUoutMEM, bit_extender_1_out, bit_extender_2_out,
       bit_extender_3_out, DinWB, DoutEX, DoutID, DoutMEM, DoutWB, ex_mem_1_aluoutmem, ex_mem_1_irmem,
       ex_mem_1_pcplus4mem, ex_mem_1_r2mem, id_ex_1_immex, id_ex_1_irex, id_ex_1_pcplus4ex, id_ex_1_r1ex,
       id_ex_1_r2ex, if_id_1_irid, if_id_1_pcplus4id, main_1_reg1, main_1_reg2_2, mem_wb_1_aluouwb,
       mem_wb_1_memoutwb, mem_wb_1_pcplus4wb, multiplexer_2_out, multiplexer_3_out, multiplexer_5_out,
       multiplexer_7_out, multiplexer_11_out, multiplexer_12_out, multiplexer_14_out, multiplexer_15_out,
       multiplexer_16_out, multiplexer_18_out, multiplexer_19_out, multiplexer_20_out, multiplexer_21_out,
       multiplexer_23_out, multiplexer_24_out, multiplexer_25_out, multiplexer_26_out, PCEX, PCID, PCin,
       R1EX, R_R2EX, rom_1_data, rom_2_data, ShamtEX, shifter_2_out, v0;
  wire [31:1] alu_1_result;

  Hex_Digit_Display hex_digit_display_1 (.value(a0[31:28]));  // open: dp
  Hex_Digit_Display hex_digit_display_2 (.value(a0[27:24]));  // open: dp
  Button button_1 (.out(ExpSrc1));
  Hex_Digit_Display hex_digit_display_3 (.value(a0[19:16]));  // open: dp
  Hex_Digit_Display hex_digit_display_4 (.value(a0[23:20]));  // open: dp
  Clock clock_1 (.out(clock_1_out));
  Multiplexer #(.disabled(0), .enable("false")) multiplexer_1 (.in0(clock_1_out), .in1(1'b1), .out(clk), .sel(HaltWB));
  Button button_2 (.out(ExpSrc2));
  Comparator #(.width(32)) comparator_1 (.a(32'ha), .b(v0), .eq(comparator_1_eq));  // open: gt, lt
  Multiplexer #(.width(32), .disabled(0), .enable("false")) multiplexer_2 (
    .in0(multiplexer_3_out), .in1(DoutEX), .out(multiplexer_2_out), .sel(EretEX));
  // Probe on DoutEX
  // Probe on multiplexer_3_out
  Multiplexer #(.width(32), .disabled(0), .enable("false")) multiplexer_3 (
    .in0(adder_1_out), .in1(multiplexer_21_out), .out(multiplexer_3_out), .sel(BranchorJump));
  Hex_Digit_Display hex_digit_display_5 (.value(a0[15:12]));  // open: dp
  Hex_Digit_Display hex_digit_display_6 (.value(a0[11:8]));  // open: dp
  Button button_3 (.out(ExpSrc3));
  Multiplexer #(.disabled(0), .enable("false")) multiplexer_4 (
    .in0(1'b0), .in1(comparator_1_eq), .out(multiplexer_4_out), .sel(SyscallWB));
  Hex_Digit_Display hex_digit_display_7 (.value(a0[3:0]));  // open: dp
  Hex_Digit_Display hex_digit_display_8 (.value(a0[7:4]));  // open: dp
  D_Flip_Flop d_ff_1 (.clk(clk), .D(multiplexer_4_out), .Q(HaltWB));  // open: Qn, preset, en, reset
  Multiplexer #(.width(32), .disabled(0), .enable("false")) multiplexer_5 (
    .in0(multiplexer_2_out), .in1(32'h800), .out(multiplexer_5_out), .sel(HasExp));
  or or_1 (or_1_out, HasExp, EretEX);
  Counter #(.width(16), .max('hffff)) counter_1 (.Q(counter_1_q), .clk(clk));  // open: load, D, count, carry, clr
  // Probe on counter_1_q
  Register #(.width(32)) PC (.D(multiplexer_5_out), .en(enable3), .Q(PCin), .clk(clk1));  // open: clr
  Multiplexer #(.disabled(0), .enable("false")) multiplexer_6 (.in0(clk), .in1(not_1_out), .out(clk1), .sel(or_1_out));
  not not_1 (not_1_out, clk);
  Counter #(.width(16), .max('hffff)) counter_2 (
    .count(\I型ID ), .Q(counter_2_q), .clk(clk));  // open: load, D, carry, clr
  Counter #(.width(16), .max('hffff)) counter_3 (
    .count(\R型ID ), .Q(counter_3_q), .clk(clk));  // open: load, D, carry, clr
  // Probe on counter_2_q
  Demultiplexer #(.width(9), .enable("false")) demultiplexer_1 (
    .out0(demultiplexer_1_out0), .out1(demultiplexer_1_out1), .in(PCin[10:2]), .sel(PCin[11]));
  Counter #(.width(16), .max('hffff)) counter_4 (
    .count(\跳转型ID ), .Q(counter_4_q), .clk(clk));  // open: load, D, carry, clr
  // Probe on counter_4_q
  // Probe on counter_3_q
  Counter #(.width(16), .max('hffff)) counter_5 (
    .count(BranchorJump), .Q(counter_5_q), .clk(clk));  // open: load, D, carry, clr
  // Probe on counter_5_q
  Adder #(.width(32)) adder_1 (.a(PCin), .b(32'h4), .out(adder_1_out));  // open: cin, cout
  Counter #(.width(16), .max('hffff)) counter_6 (
    .count(loaduse), .Q(counter_6_q), .clk(clk));  // open: load, D, carry, clr
  // Probe on counter_6_q
  ROM #(.addrWidth(9), .dataWidth(32)) rom_1 (.addr(demultiplexer_1_out0), .data(rom_1_data));  // open: sel
  Multiplexer #(.width(32), .disabled(0), .enable("false")) multiplexer_7 (
    .in0(rom_1_data), .in1(rom_2_data), .out(multiplexer_7_out), .sel(PCin[11]));
  ROM #(.addrWidth(9), .dataWidth(32)) rom_2 (.addr(demultiplexer_1_out1), .data(rom_2_data));  // open: sel
  // Probe on {if_id_1_irid[31:13], cp0regID_num, if_id_1_irid[10:0]}
  IF_ID if_id_1 (
    .PCPlus4IF(adder_1_out), .clk(clk), .PCPlus4ID(if_id_1_pcplus4id), .enable(enable3), .clr(clr1),
    .IRIF(multiplexer_7_out), .IRID({if_id_1_irid[31:13], cp0regID_num, if_id_1_irid[10:0]}), .PCinIF(PCin),
    .PCinID(PCID));
  // Probe on cp0regID_num
  Control_Unit control_unit_1 (
    .op(if_id_1_irid[31:26]), .funct(if_id_1_irid[5:0]), .Aluop(AluopID), .Select1(select1ID), .Jal(JalID),
    .Shift(ShiftID), .We(WeID), .Select2(select2ID), .Beq(BeqID), .Bne(BneID), .J_jal(J_jalID), .Jr(JrID),
    .Sw(SwID), .Lw(LwID), .Select3(select3ID), .Syscall(SyscaID), .\跳转型 (\跳转型ID ), .\R型 (\R型ID ),
    .\I型 (\I型ID ), .Sh(ShID), .Bgez(BgezID), .Eret(EretID), ._23bit(if_id_1_irid[23]), .Mtc0(Mtc0ID),
    .Mfc0(Mfc0ID), .R1(R1), .R2(if_id_1_irid[20:16]), .R1ID(R1ID_num), .R2ID(R2ID_num),
    .WriteRegID(WriteRegID), .RW_num(RW_num));
  Multiplexer #(.width(5), .disabled(0), .enable("false")) multiplexer_8 (
    .in0(if_id_1_irid[20:16]), .in1({if_id_1_irid[15:13], cp0regID_num}), .out(multiplexer_8_out),
    .sel(select1ID));
  assign bit_extender_1_out = {{16{if_id_1_irid[15]}}, {if_id_1_irid[15:13], cp0regID_num, if_id_1_irid[10:0]}};  // Bit_Extender bit_extender_1
  assign bit_extender_2_out = {{16{1'b0}}, {if_id_1_irid[15:13], cp0regID_num, if_id_1_irid[10:0]}};  // Bit_Extender bit_extender_2
  assign bit_extender_3_out = {{27{if_id_1_irid[10]}}, if_id_1_irid[10:6]};  // Bit_Extender bit_extender_3
  Multiplexer #(.width(5), .disabled(0), .enable("false")) multiplexer_9 (
    .in0(if_id_1_irid[25:21]), .in1(if_id_1_irid[20:16]), .out(R1), .sel(ShiftID));
  Multiplexer #(.width(5), .disabled(0), .enable("false")) multiplexer_10 (
    .in0(multiplexer_8_out), .in1({5{1'b1}}), .out(RW_num), .sel(JalID));
  Multiplexer #(.width(32), .disabled(0), .enable("false")) multiplexer_11 (
    .in0(bit_extender_1_out), .in1(bit_extender_2_out), .out(multiplexer_11_out), .sel(select3ID));
  // Probe on PCEX
  CP0 cp0_1 (
    .Mtc0(Mtc0EX), .clk(clk), .ExpSrc1(ExpSrc1), .ExpSrc2(ExpSrc2), .ExpSrc3(ExpSrc3),
    .cp0regwrite(cp0regwriteEX), .R2(R_R2EX), .PCin(PCEX), .Eret(EretID), .HasExp(HasExp), .Dout(DoutID),
    .cp0regread(cp0regID_num));
  // Probe on a0
  // Probe on DoutID
  // Probe on main_1_reg1
  \CS1409_U201414810_杨卿_regfile_1_main  main_1 (
    .Reg1_num(R1), .Reg2(if_id_1_irid[20:16]), .Write_Reg_num(WriteRegWB), .Din(DinWB), .Write_Enable(WeWB),
    .Clock(clk), .Reg1(main_1_reg1), .Reg2_2(main_1_reg2_2), .a0_Value(a0), .v0_Value(v0));  // open: s2_Value, ra_Value
  // Probe on multiplexer_11_out
  // Probe on DoutID
  ID_EX id_ex_1 (
    .R1ID(main_1_reg1), .R2ID(main_1_reg2_2), .R1EX(id_ex_1_r1ex), .R2EX(id_ex_1_r2ex), .enable(enable3),
    .clr(clr2), .IMMID(multiplexer_11_out), .IMMEX(id_ex_1_immex), .ShamtID(bit_extender_3_out),
    .ShamtEX(ShamtEX), .PCPlus4ID(if_id_1_pcplus4id), .PCPlus4EX(id_ex_1_pcplus4ex), .clk(clk),
    .JalID(JalID), .JalEX(id_ex_1_jalex), .LwID(LwID), .LwEX(LwEX), .SwID(SwID), .SwEX(id_ex_1_swex),
    .ShID(ShID), .ShEX(id_ex_1_shex), .select2ID(select2ID), .select2EX(select2EX), .J_jalID(J_jalID),
    .J_jalEX(J_jalEX), .ShiftID(ShiftID), .ShiftEX(ShiftEX), .BeqID(BeqID), .BeqEX(BeqEX), .AluopID(AluopID),
    .AluopEX(AluopEX), .BneID(BneID), .BneEX(BneEX), .JrID(JrID), .JrEX(JrEX), .BgezID(BgezID),
    .BgezEX(BgezEX), .WriteRegID(WriteRegID), .WriteRegEX(WriteRegEX), .WeID(WeID), .WeEX(id_ex_1_weex),
    .IRID({if_id_1_irid[31:13], cp0regID_num, if_id_1_irid[10:0]}), .IREX(id_ex_1_irex), .SyscallID(SyscaID),
    .SyscallEX(id_ex_1_syscallex), .RedrectR1MEM_num(RedrectR1MEM_num), .RedrectR1MEM(RedrectR1MEM),
    .RedrectR2MEM_num(RedrectR2MEM_num), .RedrectR2MEM(RedrectR2MEM), .RedrectR1WB_num(RedrectR1WB_num),
    .RedrectR1WB(RedrectR1WB), .RedrectR2WB_num(RedrectR2WB_num), .RedrectR2WB(RedrectR2WB), .Mtc0ID(Mtc0ID),
    .Mtc0EX(Mtc0EX), .MfcID(Mfc0ID), .MfcEX(Mfc0EX), .EretID(EretID), .EretEX(EretEX),
    .cp0regwriteID(cp0regID_num), .cp0regwriteEX(cp0regwriteEX), .DoutID(DoutID), .DoutEX(DoutEX),
    .PCinID(PCID), .PCinEX(PCEX));
  // Probe on cp0regwriteEX
  // Probe on PCEX
  // Probe on DoutEX
  Multiplexer #(.width(32), .disabled(0), .enable("false")) multiplexer_12 (
    .in0(id_ex_1_r2ex), .in1(DinWB), .out(multiplexer_12_out), .sel(RedrectR2WB));
  Hazard_Unit hazard_unit_1 (
    .WriteRegWB(WriteRegMEM), .WriteRegMEM(WriteRegEX), .R1EX_num(R1ID_num), .R2EX_num(R2ID_num),
    .enable3(enable3), .RedrectR1MEM(RedrectR1MEM_num), .RedrectR2MEM(RedrectR2MEM_num),
    .RedrectR1WB(RedrectR1WB_num), .RedrectR2WB(RedrectR2WB_num), .LwMEM(LwEX), .clk(clk),
    .BranchorJump(BJEEX), .clr1(clr1), .loaduse(loaduse), .clr2(clr2));
  Multiplexer #(.width(32), .disabled(0), .enable("false")) multiplexer_13 (
    .in0(multiplexer_12_out), .in1(ALUoutMEM), .out(R_R2EX), .sel(RedrectR2MEM));
  Multiplexer #(.width(32), .disabled(0), .enable("false")) multiplexer_14 (
    .in0(R_R2EX), .in1(id_ex_1_immex), .out(multiplexer_14_out), .sel(select2EX));
  // Probe on R_R2EX
  Shifter #(.width(28)) shifter_1 (.in(id_ex_1_irex[27:0]), .\dist (5'b00010), .out(shifter_1_out));
  Shifter #(.width(32)) shifter_2 (.in(id_ex_1_immex), .\dist (5'b00010), .out(shifter_2_out));
  and and_1 (and_1_out, BeqEX, ZeroEX);
  and and_2 (and_2_out, ~ZeroEX, BneEX);  // AND_Gate
  and and_3 (and_3_out, geEX, BgezEX);
  Multiplexer #(.width(32), .disabled(0), .enable("false")) multiplexer_15 (
    .in0(id_ex_1_r1ex), .in1(DinWB), .out(multiplexer_15_out), .sel(RedrectR1WB));
  Multiplexer #(.width(32), .disabled(0), .enable("false")) multiplexer_16 (
    .in0(multiplexer_14_out), .in1(ShamtEX), .out(multiplexer_16_out), .sel(ShiftEX));
  Adder #(.width(32)) adder_2 (.a(id_ex_1_pcplus4ex), .b(shifter_2_out), .out(adder_2_out));  // open: cin, cout
  or or_2 (or_2_out, and_1_out, and_2_out);
  or or_3 (BranchSuccessEX, or_2_out, and_3_out);
  Multiplexer #(.width(32), .disabled(0), .enable("false")) multiplexer_17 (
    .in0(multiplexer_15_out), .in1(ALUoutMEM), .out(R1EX), .sel(RedrectR1MEM));
  Multiplexer #(.width(32), .disabled(0), .enable("false")) multiplexer_18 (
    .in0(multiplexer_16_out), .in1({32{1'b0}}), .out(multiplexer_18_out), .sel(BgezEX));
  Multiplexer #(.width(32), .disabled(0), .enable("false")) multiplexer_19 (
    .in0(id_ex_1_pcplus4ex), .in1(adder_2_out), .out(multiplexer_19_out), .sel(BranchSuccessEX));
  or or_4 (BranchorJump, JrEX, J_jalEX, BranchSuccessEX);
  // Probe on R1EX
  ALU alu_1 (
    .AluOP(AluopEX), .X(R1EX), .Equal(ZeroEX), .Result({alu_1_result, geEX}), .Y(multiplexer_18_out));  // open: Signed_Overflow, Result_2, UnSigned_Overflow
  Multiplexer #(.width(32), .disabled(0), .enable("false")) multiplexer_20 (
    .in0(multiplexer_19_out), .in1({id_ex_1_pcplus4ex[31:28], shifter_1_out}), .out(multiplexer_20_out),
    .sel(J_jalEX));
  or or_5 (BJEEX, EretEX, BranchorJump);
  // Probe on {alu_1_result, geEX}
  Multiplexer #(.width(32), .disabled(0), .enable("false")) multiplexer_21 (
    .in0(multiplexer_20_out), .in1(R1EX), .out(multiplexer_21_out), .sel(JrEX));
  EX_MEM ex_mem_1 (
    .LwEX(LwEX), .ALUOUTEX({alu_1_result, geEX}), .JalEX(id_ex_1_jalex), .R2EX(R_R2EX), .ShEX(id_ex_1_shex),
    .SwEX(id_ex_1_swex), .LwMEM(LwMEM),
    .ALUOUTMEM({ex_mem_1_aluoutmem[31:2], HighMEM, ex_mem_1_aluoutmem[0]}), .JalMEM(ex_mem_1_jalmem),
    .R2MEM(ex_mem_1_r2mem), .ShMEM(ShMEM), .SwMEM(SwMEM), .clk(clk), .enable(1'b1), .clr(1'b0),
    .PCPlus4EX(id_ex_1_pcplus4ex), .PCPlus4MEM(ex_mem_1_pcplus4mem), .IREX(id_ex_1_irex),
    .IRMEM(ex_mem_1_irmem), .WeEX(id_ex_1_weex), .WeEX_2(ex_mem_1_weex_2), .SyscallEX(id_ex_1_syscallex),
    .SyscallMEM(ex_mem_1_syscallmem), .WriteRegID(WriteRegEX), .WriteRegEX(WriteRegMEM), .Mfc0EX(Mfc0EX),
    .Mfc0MEM(Mfc0MEM), .DoutEX(DoutEX), .DoutMEM(DoutMEM));
  Multiplexer #(.width(32), .disabled(0), .enable("false")) multiplexer_22 (
    .in0({ex_mem_1_aluoutmem[31:2], HighMEM, ex_mem_1_aluoutmem[0]}), .in1(DoutMEM), .out(ALUoutMEM),
    .sel(Mfc0MEM));
  // Probe on {ex_mem_1_aluoutmem[31:2], HighMEM, ex_mem_1_aluoutmem[0]}
  Multiplexer #(.width(32), .disabled(0), .enable("false")) multiplexer_23 (
    .in0(ex_mem_1_r2mem), .in1(multiplexer_24_out), .out(multiplexer_23_out), .sel(ShMEM));
  // Probe on multiplexer_23_out
  Multiplexer #(.width(32), .disabled(0), .enable("false")) multiplexer_24 (
    .in0({ram_1_data_2, ex_mem_1_r2mem[15:0]}), .in1({ex_mem_1_r2mem[15:0], ram_1_data}),
    .out(multiplexer_24_out), .sel(HighMEM));
  RAM #(.addrWidth(10), .dataWidth(32), .bus("separate")) ram_1 (
    .addr(ex_mem_1_aluoutmem[11:2]), .din(multiplexer_23_out), .data({ram_1_data_2, ram_1_data}),
    .str(SwMEM), .clk(clk), .ld(LwMEM));  // open: sel, clr
  MEM_WB mem_wb_1 (
    .clk(clk), .LwMEM(LwMEM), .LwWB(LwWB),
    .ALUOUTMEM({ex_mem_1_aluoutmem[31:2], HighMEM, ex_mem_1_aluoutmem[0]}), .ALUOUWB(mem_wb_1_aluouwb),
    .JalMEM(ex_mem_1_jalmem), .JalWB(JalWB), .MemOUTMEM({ram_1_data_2, ram_1_data}),
    .MemOUTWB(mem_wb_1_memoutwb), .PCPlus4MEM(ex_mem_1_pcplus4mem), .PCPlus4WB(mem_wb_1_pcplus4wb),
    .enable(1'b1), .clr(1'b0), .IRMEM(ex_mem_1_irmem), .WeMEM(ex_mem_1_weex_2), .WeWB(WeWB),
    .WriteRegMEM(WriteRegMEM), .WriteRegWB(WriteRegWB), .SyscallMEM(ex_mem_1_syscallmem),
    .SyscallWB(SyscallWB), .Mfc0MEM(Mfc0MEM), .Mfc0WB(Mfc0WB), .DoutMEM(DoutMEM), .DoutWB(DoutWB));  // open: IRWB
  // Probe on WriteRegWB
  Multiplexer #(.width(32), .disabled(0), .enable("false")) multiplexer_25 (
    .in0(mem_wb_1_aluouwb), .in1(mem_wb_1_memoutwb), .out(multiplexer_25_out), .sel(LwWB));
  Multiplexer #(.width(32), .disabled(0), .enable("false")) multiplexer_26 (
    .in0(multiplexer_25_out), .in1(mem_wb_1_pcplus4wb), .out(multiplexer_26_out), .sel(JalWB));
  Multiplexer #(.width(32), .disabled(0), .enable("false")) multiplexer_27 (
    .in0(multiplexer_26_out), .in1(DoutWB), .out(DinWB), .sel(Mfc0WB));
  // Probe on DinWB

  // Notes on the sheet:
  //   总周期数
  //   分支冲突
  //   loaduse冲突
  //   contents of rom_1 (hex, n*v repeats v):
  //   20110001 8000c05 20110001 20120002 20130003 8000c09 20110001 20120002 20130003 8000c0d 20110001
  //   20120002 20130003 8000c11 20110001 20120002 20130003 c000cb8 20100001 20110001 118fc0 112020
  //   20020022 c 118882 12200001 8000c15 112020 20020022 c 20110001 118880 112020 20020022 c 12200001
  //   8000c1f 20110001 118fc0 112020 20020022 c 1188c3 112020 20020022 c 118903 112020 20020022 c 118903
  //   112020 20020022 c 118903 112020 20020022 c 118903 112020 20020022 c 118903 112020 20020022 c 118903
  //   112020 20020022 c 118903 112020 20020022 c 20100001 109fc0 139fc3 8021 2012000c 24160003 26100001
  //   3210000f 20080008 20090001 139900 2709825 132020 20020022 c 1094022 1500fff9 22100001 2018000f
  //   2188024 108700 20080008 20090001 139902 2709825 132021 20020022 c 1094022 1500fff9 108702 2c9b022
  //   12c00001 8000c50 4020 1084027 84400 3508ffff 82021 20020022 c 2010ffff 20110000 ae300000 22100001
  //   22310004 ae300000 22100001 22310004 ae300000 22100001 22310004 ae300000 22100001 22310004 ae300000
  //   22100001 22310004 ae300000 22100001 22310004 ae300000 22100001 22310004 ae300000 22100001 22310004
  //   ae300000 22100001 22310004 ae300000 22100001 22310004 ae300000 22100001 22310004 ae300000 22100001
  //   22310004 ae300000 22100001 22310004 ae300000 22100001 22310004 ae300000 22100001 22310004 ae300000
  //   22100001 22310004 22100001 8020 2011003c 8e130000 8e340000 274402a 11000002 ae330000 ae140000
  //   2231fffc 1611fff8 102020 20020022 c 22100004 2011003c 1611fff2 2002000a c 20100000 22100001 102020
  //   20020022 c 22100002 102020 20020022 c 22100003 102020 20020022 c 22100004 102020 20020022 c 22100005
  //   102020 20020022 c 22100006 102020 20020022 c 22100007 102020 20020022 c 22100008 102020 20020022
  //   20020022 c 3e00008
  //   contents of rom_2 (hex, n*v repeats v):
  //   201a0001 409a6000 201c0800 39de020 401b7000 af9b0000 239cfffc af840000 239cfffc af910000 239cfffc
  //   af920000 239cfffc af930000 239cfffc af940000 239cfffc 201d0800 39de822 40146800 d020 409a6000 2020
  //   8820 9020 9820 20130001 148f00 20120004 142020 42100 1491fffe 2539022 1640fffb 201a0001 409a6000
  //   239c0004 8f940000 239c0004 8f930000 239c0004 8f920000 239c0004 8f910000 239c0004 8f840000 239c0004
  //   8f9b0000 409b7000 40946800 d020 409a6000 42000018
  //   Funct
  //   23bit
  //   Op
  //   ShamtID
  //   IMMID
endmodule

module Control_Unit (
  input  [4:0] R1,
  input  [4:0] R2,
  input  [4:0] RW_num,
  input  [5:0] op,
  input  [5:0] funct,
  input  _23bit,
  output [4:0] R1ID,
  output [4:0] R2ID,
  output [4:0] WriteRegID,
  output Select1,
  output Jal,
  output Shift,
  output Select2,
  output Beq,
  output Bne,
  output J_jal,
  output Jr,
  output Sw,
  output Lw,
  output Select3,
  output Syscall,
  output Sh,
  output Bgez,
  output \跳转型 ,
  output \R型 ,
  output \I型 ,
  output Eret,
  output Mtc0,
  output Mfc0,
  output We,
  output [3:0] Aluop
);

  wire or_15_out, or_16_out, signal2_1_j, signal2_1_lw, signal2_1_nor, signal2_1_slt, signal2_1_slti,
       signal2_1_sltu, signal2_1_sw, signal3_1_cp0, signal3_1_sltiu, signal3_1_xori, signal_1_add,
       signal_1_addi, signal_1_addiu, signal_1_addu, signal_1_and, signal_1_andi, signal_1_or, signal_1_ori,
       signal_1_sll, signal_1_sra, signal_1_srl, signal_1_sub;

  signal signal_1 (
    .op0(op[0]), .op1(op[1]), .op2(op[2]), .op3(op[3]), .op4(op[4]), .op5(op[5]), .funct0(funct[0]),
    .funct1(funct[1]), .funct2(funct[2]), .funct3(funct[3]), .funct4(funct[4]), .funct5(funct[5]),
    .add(signal_1_add), .addi(signal_1_addi), .addiu(signal_1_addiu), .addu(signal_1_addu),
    .\and (signal_1_and), .andi(signal_1_andi), .sll(signal_1_sll), .sra(signal_1_sra), .srl(signal_1_srl),
    .sub(signal_1_sub), .\or (signal_1_or), .ori(signal_1_ori));
  signal2 signal2_1 (
    .op0(op[0]), .op1(op[1]), .op2(op[2]), .op3(op[3]), .op4(op[4]), .op5(op[5]), .funct0(funct[0]),
    .funct1(funct[1]), .funct2(funct[2]), .funct3(funct[3]), .funct4(funct[4]), .funct5(funct[5]),
    .\nor (signal2_1_nor), .lw(signal2_1_lw), .sw(signal2_1_sw), .beq(Beq), .bne(Bne), .slt(signal2_1_slt),
    .slti(signal2_1_slti), .sltu(signal2_1_sltu), .j(signal2_1_j), .jal(Jal), .jr(Jr), .syscall(Syscall));
  signal3 signal3_1 (
    .op0(op[0]), .op1(op[1]), .op2(op[2]), .op3(op[3]), .op4(op[4]), .op5(op[5]), .xori(signal3_1_xori),
    .sltiu(signal3_1_sltiu), .sh(Sh), .bgez(Bgez), .cp0(signal3_1_cp0));
  or or_1 (Aluop[3], signal_1_or, signal_1_ori, signal2_1_nor, signal2_1_slt, signal2_1_slti, signal2_1_sltu, signal3_1_xori, signal3_1_sltiu, Bgez);
  or or_2 (Aluop[2], signal_1_add, signal_1_addi, signal_1_addiu, signal_1_addu, signal_1_and, signal_1_andi, signal_1_sub, signal2_1_lw, signal2_1_sw, signal2_1_sltu, signal3_1_sltiu, Sh);
  or or_3 (Aluop[1], signal_1_and, signal_1_andi, signal_1_srl, signal_1_sub, signal2_1_nor, signal2_1_slt, signal2_1_slti, Bgez);
  or or_4 (Aluop[0], signal_1_add, signal_1_addi, signal_1_addiu, signal_1_addu, signal_1_and, signal_1_andi, signal_1_sra, signal2_1_lw, signal2_1_sw, signal2_1_slt, signal2_1_slti, signal3_1_xori, Sh, Bgez);
  or or_5 (Select1, signal_1_add, signal_1_addu, signal_1_and, signal_1_sll, signal_1_sra, signal_1_srl, signal_1_sub, signal_1_or, signal2_1_nor, signal2_1_slt, signal2_1_sltu);
  or or_6 (Shift, signal_1_sll, signal_1_sra, signal_1_srl);
  nor nor_1 (We, signal2_1_sw, Beq, Bne, signal2_1_j, Jr, Syscall, Sh, Bgez, Eret, Mtc0);
  or or_7 (Select2, signal_1_addi, signal_1_addiu, signal_1_andi, signal_1_ori, signal2_1_lw, signal2_1_sw, signal2_1_slti, signal3_1_xori, signal3_1_sltiu, Sh);
  or or_8 (J_jal, signal2_1_j, Jal);
  or or_9 (Sw, signal2_1_sw, Sh);
  or or_10 (Lw, signal2_1_lw, Sh);
  or or_11 (Select3, signal_1_andi, signal_1_ori, signal3_1_xori);
  or or_12 (\跳转型 , Jal, Jr, signal2_1_j, Bgez);
  or or_13 (\R型 , signal_1_add, signal_1_addu, signal_1_and, signal_1_sll, signal_1_sra, signal_1_srl, signal_1_sub, signal_1_or, signal2_1_nor, signal2_1_slt, signal2_1_sltu, Jr, Syscall);
  or or_14 (\I型 , signal_1_addi, signal_1_addiu, signal_1_andi, signal_1_ori, signal2_1_lw, signal2_1_sw, Beq, Bne, signal2_1_slti, signal3_1_xori, signal3_1_sltiu, Sh, Bgez);
  and and_1 (Eret, signal3_1_cp0, funct[4]);
  Multiplexer #(.width(5), .disabled(0), .enable("false")) multiplexer_1 (
    .in0({5{1'b0}}), .in1(R1), .out(R1ID), .sel(or_15_out));
  or or_15 (or_15_out, signal_1_add, signal_1_addi, signal_1_addiu, signal_1_addu, signal_1_and, signal_1_andi, signal_1_sll, signal_1_sra, signal_1_srl, signal_1_sub, signal_1_or, signal_1_ori, signal2_1_nor, signal2_1_lw, signal2_1_sw, Beq, Bne, signal2_1_slt, signal2_1_slti, signal2_1_sltu, Jr, signal3_1_xori, signal3_1_sltiu, Sh, Bgez);
  and and_2 (Mfc0, ~_23bit, signal3_1_cp0, ~funct[4]);  // AND_Gate
  and and_3 (Mtc0, _23bit, signal3_1_cp0);
  Multiplexer #(.width(5), .disabled(0), .enable("false")) multiplexer_2 (
    .in0({5{1'b0}}), .in1(R2), .out(R2ID), .sel(or_16_out));
  or or_16 (or_16_out, signal_1_add, signal_1_addu, signal_1_and, signal_1_sub, signal_1_or, signal2_1_nor, Mtc0, signal2_1_sw, Beq, Bne, signal2_1_slt, signal2_1_sltu, Sh);
  Multiplexer #(.width(5), .disabled(0), .enable("false")) multiplexer_3 (
    .in0({5{1'b0}}), .in1(RW_num), .out(WriteRegID), .sel(We));
endmodule

module signal (
  input  op0,
  input  op1,
  input  op2,
  input  op3,
  input  op4,
  input  op5,
  input  funct0,
  input  funct1,
  input  funct2,
  input  funct3,
  input  funct4,
  input  funct5,
  output add,
  output addi,
  output addiu,
  output addu,
  output \and ,
  output andi,
  output sll,
  output sra,
  output srl,
  output sub,
  output \or ,
  output ori
);

  wire not_1_out, not_2_out, not_3_out, not_4_out, not_5_out, not_6_out, not_7_out, not_8_out, not_9_out,
       not_10_out, not_11_out, not_12_out, not_13_out, not_14_out, not_15_out, not_16_out, not_17_out,
       not_18_out, not_19_out, not_20_out, not_21_out, not_22_out, not_23_out, not_24_out, not_25_out,
       not_26_out, not_27_out, not_28_out, not_29_out, not_30_out, not_31_out, not_32_out, not_33_out,
       not_34_out, not_35_out, not_36_out, not_37_out, not_38_out, not_39_out, not_40_out, not_41_out,
       not_42_out, not_43_out, not_44_out, not_45_out, not_46_out, not_47_out, not_48_out, not_49_out,
       not_50_out, not_51_out, not_52_out, not_53_out, not_54_out, not_55_out, not_56_out, not_57_out,
       not_58_out, not_59_out, not_60_out, not_61_out, not_62_out, not_63_out, not_64_out, not_65_out,
       not_66_out, not_67_out, not_68_out, not_69_out, not_70_out, not_71_out, not_72_out, not_73_out,
       not_74_out, not_75_out, not_76_out, not_77_out, not_78_out, not_79_out, not_80_out, not_81_out,
       not_82_out, not_83_out, not_84_out, not_85_out, not_86_out, not_87_out, not_88_out, not_89_out,
       not_90_out, not_91_out, not_92_out, not_93_out, not_94_out, not_95_out, not_96_out, not_97_out,
       not_98_out, not_99_out;

  not not_1 (not_1_out, funct4);
  not not_2 (not_2_out, funct3);
  not not_3 (not_3_out, funct2);
  not not_4 (not_4_out, funct1);
  not not_5 (not_5_out, funct0);
  not not_6 (not_6_out, op5);
  not not_7 (not_7_out, op4);
  not not_8 (not_8_out, op3);
  not not_9 (not_9_out, op2);
  not not_10 (not_10_out, op1);
  not not_11 (not_11_out, op0);
  not not_12 (not_12_out, op5);
  not not_13 (not_13_out, op4);
  not not_14 (not_14_out, op2);
  not not_15 (not_15_out, op1);
  not not_16 (not_16_out, op0);
  not not_17 (not_17_out, op5);
  not not_18 (not_18_out, op4);
  not not_19 (not_19_out, op2);
  not not_20 (not_20_out, op1);
  not not_21 (not_21_out, funct4);
  not not_22 (not_22_out, funct3);
  not not_23 (not_23_out, funct2);
  not not_24 (not_24_out, funct1);
  not not_25 (not_25_out, op5);
  not not_26 (not_26_out, op4);
  not not_27 (not_27_out, op3);
  not not_28 (not_28_out, op2);
  not not_29 (not_29_out, op1);
  not not_30 (not_30_out, op0);
  not not_31 (not_31_out, funct4);
  not not_32 (not_32_out, funct3);
  not not_33 (not_33_out, funct1);
  not not_34 (not_34_out, funct0);
  not not_35 (not_35_out, op5);
  not not_36 (not_36_out, op4);
  not not_37 (not_37_out, op3);
  not not_38 (not_38_out, op2);
  not not_39 (not_39_out, op1);
  not not_40 (not_40_out, op0);
  not not_41 (not_41_out, op5);
  not not_42 (not_42_out, op4);
  not not_43 (not_43_out, op1);
  not not_44 (not_44_out, op0);
  not not_45 (not_45_out, funct5);
  not not_46 (not_46_out, funct4);
  not not_47 (not_47_out, funct3);
  not not_48 (not_48_out, funct2);
  not not_49 (not_49_out, funct1);
  not not_50 (not_50_out, funct0);
  not not_51 (not_51_out, op5);
  not not_52 (not_52_out, op4);
  not not_53 (not_53_out, op3);
  not not_54 (not_54_out, op2);
  not not_55 (not_55_out, op1);
  not not_56 (not_56_out, op0);
  not not_57 (not_57_out, funct5);
  not not_58 (not_58_out, funct4);
  not not_59 (not_59_out, funct3);
  not not_60 (not_60_out, funct2);
  not not_61 (not_61_out, op5);
  not not_62 (not_62_out, op4);
  not not_63 (not_63_out, op3);
  not not_64 (not_64_out, op2);
  not not_65 (not_65_out, op1);
  not not_66 (not_66_out, op0);
  not not_67 (not_67_out, funct5);
  not not_68 (not_68_out, funct4);
  not not_69 (not_69_out, funct3);
  not not_70 (not_70_out, funct2);
  not not_71 (not_71_out, funct0);
  not not_72 (not_72_out, op5);
  not not_73 (not_73_out, op4);
  not not_74 (not_74_out, op3);
  not not_75 (not_75_out, op2);
  not not_76 (not_76_out, op1);
  not not_77 (not_77_out, op0);
  not not_78 (not_78_out, funct4);
  not not_79 (not_79_out, funct3);
  not not_80 (not_80_out, funct2);
  not not_81 (not_81_out, funct0);
  not not_82 (not_82_out, op5);
  not not_83 (not_83_out, op4);
  not not_84 (not_84_out, op3);
  not not_85 (not_85_out, op2);
  not not_86 (not_86_out, op1);
  not not_87 (not_87_out, op0);
  not not_88 (not_88_out, funct4);
  not not_89 (not_89_out, funct3);
  not not_90 (not_90_out, funct1);
  not not_91 (not_91_out, op5);
  not not_92 (not_92_out, op4);
  not not_93 (not_93_out, op3);
  not not_94 (not_94_out, op2);
  not not_95 (not_95_out, op1);
  not not_96 (not_96_out, op0);
  not not_97 (not_97_out, op5);
  not not_98 (not_98_out, op4);
  not not_99 (not_99_out, op1);
  and and_1 (add, funct5, not_1_out, not_2_out, not_3_out, not_4_out, not_5_out, not_6_out, not_7_out, not_8_out, not_9_out, not_10_out, not_11_out);
  and and_2 (addi, not_12_out, not_13_out, op3, not_14_out, not_15_out, not_16_out);
  and and_3 (addiu, not_17_out, not_18_out, op3, not_19_out, not_20_out, op0);
  and and_4 (addu, funct5, not_21_out, not_22_out, not_23_out, not_24_out, funct0, not_25_out, not_26_out, not_27_out, not_28_out, not_29_out, not_30_out);
  and and_5 (\and , funct5, not_31_out, not_32_out, funct2, not_33_out, not_34_out, not_35_out, not_36_out, not_37_out, not_38_out, not_39_out, not_40_out);
  and and_6 (andi, not_41_out, not_42_out, op3, op2, not_43_out, not_44_out);
  and and_7 (sll, not_45_out, not_46_out, not_47_out, not_48_out, not_49_out, not_50_out, not_51_out, not_52_out, not_53_out, not_54_out, not_55_out, not_56_out);
  and and_8 (sra, not_57_out, not_58_out, not_59_out, not_60_out, funct1, funct0, not_61_out, not_62_out, not_63_out, not_64_out, not_65_out, not_66_out);
  and and_9 (srl, not_67_out, not_68_out, not_69_out, not_70_out, funct1, not_71_out, not_72_out, not_73_out, not_74_out, not_75_out, not_76_out, not_77_out);
  and and_10 (sub, funct5, not_78_out, not_79_out, not_80_out, funct1, not_81_out, not_82_out, not_83_out, not_84_out, not_85_out, not_86_out, not_87_out);
  and and_11 (\or , funct5, not_88_out, not_89_out, funct2, not_90_out, funct0, not_91_out, not_92_out, not_93_out, not_94_out, not_95_out, not_96_out);
  and and_12 (ori, not_97_out, not_98_out, op3, op2, not_99_out, op0);
endmodule

module signal2 (
  input  op0,
  input  op1,
  input  op2,
  input  op3,
  input  op4,
  input  op5,
  input  funct0,
  input  funct1,
  input  funct2,
  input  funct3,
  input  funct4,
  input  funct5,
  output \nor ,
  output lw,
  output sw,
  output beq,
  output bne,
  output slt,
  output slti,
  output sltu,
  output j,
  output jal,
  output jr,
  output syscall
);

  wire not_1_out, not_2_out, not_3_out, not_4_out, not_5_out, not_6_out, not_7_out, not_8_out, not_9_out,
       not_10_out, not_11_out, not_12_out, not_13_out, not_14_out, not_15_out, not_16_out, not_17_out,
       not_18_out, not_19_out, not_20_out, not_21_out, not_22_out, not_23_out, not_24_out, not_25_out,
       not_26_out, not_27_out, not_28_out, not_29_out, not_30_out, not_31_out, not_32_out, not_33_out,
       not_34_out, not_35_out, not_36_out, not_37_out, not_38_out, not_39_out, not_40_out, not_41_out,
       not_42_out, not_43_out, not_44_out, not_45_out, not_46_out, not_47_out, not_48_out, not_49_out,
       not_50_out, not_51_out, not_52_out, not_53_out, not_54_out, not_55_out, not_56_out, not_57_out,
       not_58_out, not_59_out, not_60_out, not_61_out, not_62_out, not_63_out, not_64_out, not_65_out,
       not_66_out, not_67_out, not_68_out, not_69_out, not_70_out, not_71_out, not_72_out, not_73_out;

  not not_1 (not_1_out, funct4);
  not not_2 (not_2_out, funct3);
  not not_3 (not_3_out, op5);
  not not_4 (not_4_out, op4);
  not not_5 (not_5_out, op3);
  not not_6 (not_6_out, op2);
  not not_7 (not_7_out, op1);
  not not_8 (not_8_out, op0);
  not not_9 (not_9_out, op4);
  not not_10 (not_10_out, op3);
  not not_11 (not_11_out, op2);
  not not_12 (not_12_out, op4);
  not not_13 (not_13_out, op2);
  not not_14 (not_14_out, op5);
  not not_15 (not_15_out, op4);
  not not_16 (not_16_out, op3);
  not not_17 (not_17_out, op1);
  not not_18 (not_18_out, op0);
  not not_19 (not_19_out, op5);
  not not_20 (not_20_out, op4);
  not not_21 (not_21_out, op3);
  not not_22 (not_22_out, op1);
  not not_23 (not_23_out, funct4);
  not not_24 (not_24_out, funct2);
  not not_25 (not_25_out, funct0);
  not not_26 (not_26_out, op5);
  not not_27 (not_27_out, op4);
  not not_28 (not_28_out, op3);
  not not_29 (not_29_out, op2);
  not not_30 (not_30_out, op1);
  not not_31 (not_31_out, op0);
  not not_32 (not_32_out, op5);
  not not_33 (not_33_out, op4);
  not not_34 (not_34_out, op2);
  not not_35 (not_35_out, op0);
  not not_36 (not_36_out, funct4);
  not not_37 (not_37_out, funct2);
  not not_38 (not_38_out, op5);
  not not_39 (not_39_out, op4);
  not not_40 (not_40_out, op3);
  not not_41 (not_41_out, op2);
  not not_42 (not_42_out, op1);
  not not_43 (not_43_out, op0);
  not not_44 (not_44_out, op5);
  not not_45 (not_45_out, op4);
  not not_46 (not_46_out, op3);
  not not_47 (not_47_out, op2);
  not not_48 (not_48_out, op0);
  not not_49 (not_49_out, op5);
  not not_50 (not_50_out, op4);
  not not_51 (not_51_out, op3);
  not not_52 (not_52_out, op2);
  not not_53 (not_53_out, funct5);
  not not_54 (not_54_out, funct4);
  not not_55 (not_55_out, funct2);
  not not_56 (not_56_out, funct1);
  not not_57 (not_57_out, funct0);
  not not_58 (not_58_out, op5);
  not not_59 (not_59_out, op4);
  not not_60 (not_60_out, op3);
  not not_61 (not_61_out, op2);
  not not_62 (not_62_out, op1);
  not not_63 (not_63_out, op0);
  not not_64 (not_64_out, funct5);
  not not_65 (not_65_out, funct4);
  not not_66 (not_66_out, funct1);
  not not_67 (not_67_out, funct0);
  not not_68 (not_68_out, op5);
  not not_69 (not_69_out, op4);
  not not_70 (not_70_out, op3);
  not not_71 (not_71_out, op2);
  not not_72 (not_72_out, op1);
  not not_73 (not_73_out, op0);
  and and_1 (\nor , funct5, not_1_out, not_2_out, funct2, funct1, funct0, not_3_out, not_4_out, not_5_out, not_6_out, not_7_out, not_8_out);
  and and_2 (lw, op5, not_9_out, not_10_out, not_11_out, op1, op0);
  and and_3 (sw, op5, not_12_out, op3, not_13_out, op1, op0);
  and and_4 (beq, not_14_out, not_15_out, not_16_out, op2, not_17_out, not_18_out);
  and and_5 (bne, not_19_out, not_20_out, not_21_out, op2, not_22_out, op0);
  and and_6 (slt, funct5, not_23_out, funct3, not_24_out, funct1, not_25_out, not_26_out, not_27_out, not_28_out, not_29_out, not_30_out, not_31_out);
  and and_7 (slti, not_32_out, not_33_out, op3, not_34_out, op1, not_35_out);
  and and_8 (sltu, funct5, not_36_out, funct3, not_37_out, funct1, funct0, not_38_out, not_39_out, not_40_out, not_41_out, not_42_out, not_43_out);
  and and_9 (j, not_44_out, not_45_out, not_46_out, not_47_out, op1, not_48_out);
  and and_10 (jal, not_49_out, not_50_out, not_51_out, not_52_out, op1, op0);
  and and_11 (jr, not_53_out, not_54_out, funct3, not_55_out, not_56_out, not_57_out, not_58_out, not_59_out, not_60_out, not_61_out, not_62_out, not_63_out);
  and and_12 (syscall, not_64_out, not_65_out, funct3, funct2, not_66_out, not_67_out, not_68_out, not_69_out, not_70_out, not_71_out, not_72_out, not_73_out);
endmodule

module signal3 (
  input  op0,
  input  op1,
  input  op2,
  input  op3,
  input  op4,
  input  op5,
  output xori,
  output sltiu,
  output sh,
  output bgez,
  output cp0
);

  wire not_1_out, not_2_out, not_3_out, not_4_out, not_5_out, not_6_out, not_7_out, not_8_out, not_9_out,
       not_10_out, not_11_out, not_12_out, not_13_out, not_14_out, not_15_out, not_16_out, not_17_out,
       not_18_out, not_19_out;

  not not_1 (not_1_out, op5);
  not not_2 (not_2_out, op4);
  not not_3 (not_3_out, op0);
  not not_4 (not_4_out, op5);
  not not_5 (not_5_out, op4);
  not not_6 (not_6_out, op2);
  not not_7 (not_7_out, op4);
  not not_8 (not_8_out, op2);
  not not_9 (not_9_out, op1);
  not not_10 (not_10_out, op5);
  not not_11 (not_11_out, op4);
  not not_12 (not_12_out, op3);
  not not_13 (not_13_out, op2);
  not not_14 (not_14_out, op1);
  not not_15 (not_15_out, op5);
  not not_16 (not_16_out, op3);
  not not_17 (not_17_out, op2);
  not not_18 (not_18_out, op1);
  not not_19 (not_19_out, op0);
  and and_1 (xori, not_1_out, not_2_out, op3, op2, op1, not_3_out);
  and and_2 (sltiu, not_4_out, not_5_out, op3, not_6_out, op1, op0);
  and and_3 (sh, op5, not_7_out, op3, not_8_out, not_9_out, op0);
  and and_4 (bgez, not_10_out, not_11_out, not_12_out, not_13_out, not_14_out, op0);
  and and_5 (cp0, not_15_out, op4, not_16_out, not_17_out, not_18_out, not_19_out);
endmodule

module CP0 (
  input  [31:0] R2,
  input  [31:0] PCin,
  input  Mtc0,
  input  Eret,
  input  [1:0] cp0regread,
  input  [1:0] cp0regwrite,
  input  clk,
  input  ExpSrc1,
  input  ExpSrc2,
  input  ExpSrc3,
  output [31:0] Dout,
  output HasExp
);

  wire and_1_out, and_2_out, and_3_out, and_4_out, and_5_out, and_6_out, clr, comparator_1_eq, d_ff_1_q,
       d_ff_2_q, d_ff_3_q, demultiplexer_1_out0, demultiplexer_1_out1, demultiplexer_1_out2,
       demultiplexer_2_out1, demultiplexer_2_out2, demultiplexer_2_out3, IE, IR1_q, IR2_q, IR3_q, not_1_out,
       not_2_out, or_1_out, or_2_out;
  wire [1:0] pri, priority_encoder_1_out, shield;
  wire [31:0] cause, EPC_q, multiplexer_1_out, multiplexer_2_out, multiplexer_3_out, status_q;
  wire [31:2] cause_q;

  Demultiplexer #(.select(2), .disabled(0), .enable("false")) demultiplexer_1 (
    .out0(demultiplexer_1_out0), .out1(demultiplexer_1_out1), .out2(demultiplexer_1_out2), .in(Mtc0),
    .sel(cp0regwrite));  // open: out3
  Multiplexer #(.width(32), .disabled(0), .enable("false")) multiplexer_1 (
    .in0(R2), .in1(PCin), .out(multiplexer_1_out), .sel(HasExp));
  or or_1 (or_1_out, HasExp, demultiplexer_1_out1);
  or or_2 (or_2_out, HasExp, demultiplexer_1_out2);
  not not_1 (not_1_out, comparator_1_eq);
  Comparator #(.width(32), .mode("unsigned")) comparator_1 (
    .a(PCin), .b({32{1'b0}}), .eq(comparator_1_eq));  // open: gt, lt
  D_Flip_Flop d_ff_1 (.clk(ExpSrc1), .D(1'b1), .Q(d_ff_1_q), .reset(demultiplexer_2_out1));  // open: Qn, preset, en
  D_Flip_Flop d_ff_2 (.clk(ExpSrc2), .D(1'b1), .Q(d_ff_2_q), .reset(demultiplexer_2_out2));  // open: Qn, preset, en
  and and_1 (and_1_out, d_ff_2_q, not_1_out);
  D_Flip_Flop d_ff_3 (.clk(ExpSrc3), .D(1'b1), .Q(d_ff_3_q), .reset(demultiplexer_2_out3));  // open: Qn, preset, en
  and and_2 (and_2_out, d_ff_3_q, not_1_out);
  Multiplexer #(.width(32), .disabled(0), .enable("false")) multiplexer_2 (
    .in0(R2), .in1(cause), .out(multiplexer_2_out), .sel(HasExp));
  and and_3 (and_3_out, d_ff_1_q, not_1_out);
  Demultiplexer #(.select(2), .disabled(0), .enable("false")) demultiplexer_2 (
    .out1(demultiplexer_2_out1), .out2(demultiplexer_2_out2), .out3(demultiplexer_2_out3), .in(clr), .sel(pri));  // open: out0
  Register #(.width(32), .trigger("falling")) status (
    .D(multiplexer_1_out), .en(demultiplexer_1_out0), .Q(status_q), .clk(clk));  // open: clr
  Register #(.width(32), .trigger("falling")) u_cause (
    .D(multiplexer_2_out), .en(or_1_out), .Q({cause_q, shield}), .clk(clk));  // open: clr
  Register #(.width(32), .trigger("falling")) EPC (
    .D(multiplexer_1_out), .en(or_2_out), .Q(EPC_q), .clk(clk));  // open: clr
  not not_2 (not_2_out, status_q[0]);
  Multiplexer #(.select(2), .width(32), .disabled(0), .enable("false")) multiplexer_3 (
    .in0(status_q), .in1({cause_q, shield}), .in2(EPC_q), .out(multiplexer_3_out), .sel(cp0regread));  // open: in3
  D_Flip_Flop IR1 (.clk(clk), .D(and_3_out), .Q(IR1_q), .reset(demultiplexer_2_out1));  // open: Qn, preset, en
  D_Flip_Flop IR2 (.clk(clk), .D(and_1_out), .Q(IR2_q), .reset(demultiplexer_2_out2));  // open: Qn, preset, en
  D_Flip_Flop IR3 (.clk(clk), .D(and_2_out), .Q(IR3_q), .reset(demultiplexer_2_out3));  // open: Qn, preset, en
  D_Flip_Flop #(.trigger("falling")) d_ff_4 (.clk(clk), .D(not_2_out), .Q(IE));  // open: Qn, preset, en, reset
  Multiplexer #(.width(32), .disabled(0), .enable("false")) multiplexer_4 (
    .in0(multiplexer_3_out), .in1(EPC_q), .out(Dout), .sel(Eret));
  and and_4 (and_4_out, IR1_q, IE);
  and and_5 (and_5_out, IR2_q, IE);
  and and_6 (and_6_out, IR3_q, IE);
  Priority_Encoder #(.select(2)) priority_encoder_1 (
    .in0(1'b1), .in1(and_4_out), .in2(and_5_out), .in3(and_6_out), .out(priority_encoder_1_out));  // open: gs, en_out, en_in
  // Probe on shield
  Register #(.width(2), .trigger("falling")) register_1 (
    .D(priority_encoder_1_out), .Q(pri), .clk(clk));  // open: en, clr
  assign cause = {{30{1'b0}}, priority_encoder_1_out};  // Bit_Extender bit_extender_1
  Comparator #(.width(2), .mode("unsigned")) comparator_2 (
    .a(priority_encoder_1_out), .b(shield), .gt(HasExp));  // open: eq, lt
  Register #(.width(1), .trigger("falling")) register_2 (.D(HasExp), .Q(clr), .clk(clk));  // open: en, clr
endmodule

module IF_ID (
  input  [31:0] PCinIF,
  input  [31:0] PCPlus4IF,
  input  [31:0] IRIF,
  input  clk,
  input  enable,
  input  clr,
  output [31:0] PCinID,
  output [31:0] PCPlus4ID,
  output [31:0] IRID
);

  Register #(.width(32)) register_1 (.D(PCinIF), .en(enable), .Q(PCinID), .clk(clk), .clr(clr));
  Register #(.width(32)) register_2 (.D(PCPlus4IF), .en(enable), .Q(PCPlus4ID), .clk(clk), .clr(clr));
  Register #(.width(32)) register_3 (.D(IRIF), .en(enable), .Q(IRID), .clk(clk), .clr(clr));
endmodule

module ID_EX (
  input  clk,
  input  [31:0] R1ID,
  input  SyscallID,
  input  J_jalID,
  input  WeID,
  input  ShiftID,
  input  [31:0] R2ID,
  input  JalID,
  input  BeqID,
  input  [31:0] IMMID,
  input  LwID,
  input  BgezID,
  input  SwID,
  input  [3:0] AluopID,
  input  [4:0] WriteRegID,
  input  ShID,
  input  BneID,
  input  [31:0] ShamtID,
  input  select2ID,
  input  JrID,
  input  [31:0] PCPlus4ID,
  input  RedrectR1MEM_num,
  input  RedrectR2MEM_num,
  input  [31:0] IRID,
  input  RedrectR1WB_num,
  input  RedrectR2WB_num,
  input  [1:0] cp0regwriteID,
  input  Mtc0ID,
  input  MfcID,
  input  [31:0] DoutID,
  input  EretID,
  input  [31:0] PCinID,
  input  enable,
  input  clr,
  output [31:0] R1EX,
  output SyscallEX,
  output J_jalEX,
  output WeEX,
  output ShiftEX,
  output [31:0] R2EX,
  output JalEX,
  output BeqEX,
  output [31:0] IMMEX,
  output LwEX,
  output BgezEX,
  output SwEX,
  output [3:0] AluopEX,
  output [4:0] WriteRegEX,
  output ShEX,
  output BneEX,
  output [31:0] ShamtEX,
  output select2EX,
  output JrEX,
  output [31:0] PCPlus4EX,
  output RedrectR1MEM,
  output RedrectR2MEM,
  output [31:0] IREX,
  output RedrectR1WB,
  output RedrectR2WB,
  output [1:0] cp0regwriteEX,
  output Mtc0EX,
  output MfcEX,
  output [31:0] DoutEX,
  output EretEX,
  output [31:0] PCinEX
);

  Register #(.width(32)) register_1 (.D(R1ID), .en(enable), .Q(R1EX), .clk(clk), .clr(clr));
  Register #(.width(32)) register_2 (.D(R2ID), .en(enable), .Q(R2EX), .clk(clk), .clr(clr));
  Register #(.width(32)) register_3 (.D(IMMID), .en(enable), .Q(IMMEX), .clk(clk), .clr(clr));
  Register #(.width(5)) register_4 (.D(WriteRegID), .en(enable), .Q(WriteRegEX), .clk(clk), .clr(clr));
  Register #(.width(32)) register_5 (.D(ShamtID), .en(enable), .Q(ShamtEX), .clk(clk), .clr(clr));
  Register #(.width(32)) register_6 (.D(PCPlus4ID), .en(enable), .Q(PCPlus4EX), .clk(clk), .clr(clr));
  Register #(.width(32)) register_7 (.D(IRID), .en(enable), .Q(IREX), .clk(clk), .clr(clr));
  Register #(.width(2)) register_8 (.D(cp0regwriteID), .en(enable), .Q(cp0regwriteEX), .clk(clk), .clr(clr));
  Register #(.width(32)) register_9 (.D(DoutID), .en(enable), .Q(DoutEX), .clk(clk), .clr(clr));
  Register #(.width(32)) register_10 (.D(PCinID), .en(enable), .Q(PCinEX), .clk(clk), .clr(clr));
  Register #(.width(1)) register_11 (.D(SyscallID), .en(enable), .Q(SyscallEX), .clk(clk), .clr(clr));
  Register #(.width(1)) register_12 (.D(WeID), .en(enable), .Q(WeEX), .clk(clk), .clr(clr));
  Register #(.width(1)) register_13 (.D(JalID), .en(enable), .Q(JalEX), .clk(clk), .clr(clr));
  Register #(.width(1)) register_14 (.D(LwID), .en(enable), .Q(LwEX), .clk(clk), .clr(clr));
  Register #(.width(1)) register_15 (.D(SwID), .en(enable), .Q(SwEX), .clk(clk), .clr(clr));
  Register #(.width(1)) register_16 (.D(ShID), .en(enable), .Q(ShEX), .clk(clk), .clr(clr));
  Register #(.width(1)) register_17 (.D(select2ID), .en(enable), .Q(select2EX), .clk(clk), .clr(clr));
  Register #(.width(1)) register_18 (.D(RedrectR1MEM_num), .en(enable), .Q(RedrectR1MEM), .clk(clk), .clr(clr));
  Register #(.width(1)) register_19 (.D(RedrectR1WB_num), .en(enable), .Q(RedrectR1WB), .clk(clk), .clr(clr));
  Register #(.width(1)) register_20 (.D(Mtc0ID), .en(enable), .Q(Mtc0EX), .clk(clk), .clr(clr));
  Register #(.width(1)) register_21 (.D(EretID), .en(enable), .Q(EretEX), .clk(clk), .clr(clr));
  Register #(.width(1)) register_22 (.D(J_jalID), .en(enable), .Q(J_jalEX), .clk(clk), .clr(clr));
  Register #(.width(1)) register_23 (.D(ShiftID), .en(enable), .Q(ShiftEX), .clk(clk), .clr(clr));
  Register #(.width(1)) register_24 (.D(BeqID), .en(enable), .Q(BeqEX), .clk(clk), .clr(clr));
  Register #(.width(1)) register_25 (.D(BgezID), .en(enable), .Q(BgezEX), .clk(clk), .clr(clr));
  Register #(.width(4)) register_26 (.D(AluopID), .en(enable), .Q(AluopEX), .clk(clk), .clr(clr));
  Register #(.width(1)) register_27 (.D(BneID), .en(enable), .Q(BneEX), .clk(clk), .clr(clr));
  Register #(.width(1)) register_28 (.D(JrID), .en(enable), .Q(JrEX), .clk(clk), .clr(clr));
  Register #(.width(1)) register_29 (.D(RedrectR2MEM_num), .en(enable), .Q(RedrectR2MEM), .clk(clk), .clr(clr));
  Register #(.width(1)) register_30 (.D(RedrectR2WB_num), .en(enable), .Q(RedrectR2WB), .clk(clk), .clr(clr));
  Register #(.width(1)) register_31 (.D(MfcID), .en(enable), .Q(MfcEX), .clk(clk), .clr(clr));
endmodule

module EX_MEM (
  input  clk,
  input  SyscallEX,
  input  [31:0] ALUOUTEX,
  input  WeEX,
  input  [31:0] R2EX,
  input  JalEX,
  input  [4:0] WriteRegID,
  input  SwEX,
  input  LwEX,
  input  [31:0] IREX,
  input  ShEX,
  input  [31:0] PCPlus4EX,
  input  Mfc0EX,
  input  [31:0] DoutEX,
  input  enable,
  input  clr,
  output SyscallMEM,
  output [31:0] ALUOUTMEM,
  output WeEX_2,
  output [31:0] R2MEM,
  output JalMEM,
  output [4:0] WriteRegEX,
  output SwMEM,
  output LwMEM,
  output [31:0] IRMEM,
  output ShMEM,
  output [31:0] PCPlus4MEM,
  output Mfc0MEM,
  output [31:0] DoutMEM
);

  Register #(.width(32)) register_1 (.D(ALUOUTEX), .en(enable), .Q(ALUOUTMEM), .clk(clk), .clr(clr));
  Register #(.width(32)) register_2 (.D(R2EX), .en(enable), .Q(R2MEM), .clk(clk), .clr(clr));
  Register #(.width(5)) register_3 (.D(WriteRegID), .en(enable), .Q(WriteRegEX), .clk(clk), .clr(clr));
  Register #(.width(32)) register_4 (.D(IREX), .en(enable), .Q(IRMEM), .clk(clk), .clr(clr));
  Register #(.width(32)) register_5 (.D(PCPlus4EX), .en(enable), .Q(PCPlus4MEM), .clk(clk), .clr(clr));
  Register #(.width(32)) register_6 (.D(DoutEX), .en(enable), .Q(DoutMEM), .clk(clk), .clr(clr));
  Register #(.width(1)) register_7 (.D(SyscallEX), .en(enable), .Q(SyscallMEM), .clk(clk), .clr(clr));
  Register #(.width(1)) register_8 (.D(WeEX), .en(enable), .Q(WeEX_2), .clk(clk), .clr(clr));
  Register #(.width(1)) register_9 (.D(JalEX), .en(enable), .Q(JalMEM), .clk(clk), .clr(clr));
  Register #(.width(1)) register_10 (.D(SwEX), .en(enable), .Q(SwMEM), .clk(clk), .clr(clr));
  Register #(.width(1)) register_11 (.D(LwEX), .en(enable), .Q(LwMEM), .clk(clk), .clr(clr));
  Register #(.width(1)) register_12 (.D(ShEX), .en(enable), .Q(ShMEM), .clk(clk), .clr(clr));
  Register #(.width(1)) register_13 (.D(Mfc0EX), .en(enable), .Q(Mfc0MEM), .clk(clk), .clr(clr));
endmodule

module MEM_WB (
  input  clk,
  input  [31:0] ALUOUTMEM,
  input  SyscallMEM,
  input  WeMEM,
  input  [31:0] MemOUTMEM,
  input  LwMEM,
  input  [4:0] WriteRegMEM,
  input  JalMEM,
  input  [31:0] IRMEM,
  input  [31:0] PCPlus4MEM,
  input  Mfc0MEM,
  input  [31:0] DoutMEM,
  input  enable,
  input  clr,
  output [31:0] ALUOUWB,
  output SyscallWB,
  output WeWB,
  output [31:0] MemOUTWB,
  output LwWB,
  output [4:0] WriteRegWB,
  output JalWB,
  output [31:0] IRWB,
  output [31:0] PCPlus4WB,
  output Mfc0WB,
  output [31:0] DoutWB
);

  Register #(.width(32)) register_1 (.D(ALUOUTMEM), .en(enable), .Q(ALUOUWB), .clk(clk), .clr(clr));
  Register #(.width(32)) register_2 (.D(MemOUTMEM), .en(enable), .Q(MemOUTWB), .clk(clk), .clr(clr));
  Register #(.width(5)) register_3 (.D(WriteRegMEM), .en(enable), .Q(WriteRegWB), .clk(clk), .clr(clr));
  Register #(.width(32)) register_4 (.D(IRMEM), .en(enable), .Q(IRWB), .clk(clk), .clr(clr));
  Register #(.width(32)) register_5 (.D(PCPlus4MEM), .en(enable), .Q(PCPlus4WB), .clk(clk), .clr(clr));
  Register #(.width(32)) register_6 (.D(DoutMEM), .en(enable), .Q(DoutWB), .clk(clk), .clr(clr));
  Register #(.width(1)) register_7 (.D(SyscallMEM), .en(enable), .Q(SyscallWB), .clk(clk), .clr(clr));
  Register #(.width(1)) register_8 (.D(WeMEM), .en(enable), .Q(WeWB), .clk(clk), .clr(clr));
  Register #(.width(1)) register_9 (.D(LwMEM), .en(enable), .Q(LwWB), .clk(clk), .clr(clr));
  Register #(.width(1)) register_10 (.D(JalMEM), .en(enable), .Q(JalWB), .clk(clk), .clr(clr));
  Register #(.width(1)) register_11 (.D(Mfc0MEM), .en(enable), .Q(Mfc0WB), .clk(clk), .clr(clr));
endmodule

module Hazard_Unit (
  input  [4:0] WriteRegWB,
  input  LwMEM,
  input  clk,
  input  [4:0] WriteRegMEM,
  input  BranchorJump,
  input  [4:0] R1EX_num,
  input  [4:0] R2EX_num,
  output clr2,
  output clr1,
  output enable3,
  output RedrectR1MEM,
  output loaduse,
  output RedrectR2MEM,
  output RedrectR1WB,
  output RedrectR2WB
);

  wire and_1_out, and_2_out, and_8_out, and_9_out, comparator_1_eq, comparator_2_eq, comparator_3_eq,
       comparator_4_eq, comparator_5_eq, comparator_6_eq, d_ff_1_q, d_ff_2_q, or_1_out;

  Comparator #(.width(5), .mode("unsigned")) comparator_1 (
    .a(WriteRegMEM), .b(R1EX_num), .eq(comparator_1_eq));  // open: gt, lt
  Comparator #(.width(5), .mode("unsigned")) comparator_2 (
    .a(WriteRegMEM), .b(R2EX_num), .eq(comparator_2_eq));  // open: gt, lt
  Comparator #(.width(5), .mode("unsigned")) comparator_3 (
    .a(WriteRegWB), .b(R1EX_num), .eq(comparator_3_eq));  // open: gt, lt
  Comparator #(.width(5), .mode("unsigned")) comparator_4 (
    .a(WriteRegWB), .b(R2EX_num), .eq(comparator_4_eq));  // open: gt, lt
  Comparator #(.width(5), .mode("unsigned")) comparator_5 (
    .a({5{1'b0}}), .b(R1EX_num), .eq(comparator_5_eq));  // open: gt, lt
  Comparator #(.width(5), .mode("unsigned")) comparator_6 (
    .a({5{1'b0}}), .b(R2EX_num), .eq(comparator_6_eq));  // open: gt, lt
  and and_1 (and_1_out, comparator_1_eq, ~comparator_5_eq);  // AND_Gate
  and and_2 (and_2_out, comparator_2_eq, ~comparator_6_eq);  // AND_Gate
  and and_3 (RedrectR1WB, comparator_3_eq, ~comparator_5_eq);  // AND_Gate
  and and_4 (RedrectR2WB, comparator_4_eq, ~comparator_6_eq);  // AND_Gate
  or or_1 (or_1_out, and_2_out, and_1_out);
  and and_5 (RedrectR1MEM, and_1_out, ~LwMEM);  // AND_Gate
  and and_6 (RedrectR2MEM, and_2_out, ~LwMEM);  // AND_Gate
  and and_7 (loaduse, LwMEM, or_1_out);
  not not_1 (enable3, loaduse);
  D_Flip_Flop #(.trigger("falling")) d_ff_1 (.clk(clk), .D(loaduse), .Q(d_ff_1_q));  // open: Qn, preset, en, reset
  and and_8 (and_8_out, clk, d_ff_1_q);
  and and_9 (and_9_out, BranchorJump, enable3);
  D_Flip_Flop #(.trigger("falling")) d_ff_2 (.clk(clk), .D(and_9_out), .Q(d_ff_2_q));  // open: Qn, preset, en, reset
  and and_10 (clr1, clk, d_ff_2_q);
  or or_2 (clr2, and_8_out, clr1);
endmodule
